// Logisim project digital clock.circ as structural Verilog: 3 circuits, main circuit main
module main (
);

  wire and_1_out, and_2_out, and_3_out, and_4_out, and_5_out, and_6_out, button_1_out, button_2_out,
       clock_1_out, n4_bit_counter_1_a0, n4_bit_counter_1_a1, n4_bit_counter_1_a2, n4_bit_counter_1_a3,
       n4_bit_counter_2_a0, n4_bit_counter_2_a1, n4_bit_counter_2_a2, n4_bit_counter_2_a3,
       n4_bit_counter_3_a0, n4_bit_counter_3_a1, n4_bit_counter_3_a2, n4_bit_counter_3_a3,
       n4_bit_counter_4_a0, n4_bit_counter_4_a1, n4_bit_counter_4_a2, n4_bit_counter_4_a3,
       n4_bit_counter_5_a0, n4_bit_counter_5_a1, n4_bit_counter_5_a2, n4_bit_counter_5_a3,
       n4_bit_counter_6_a0, n4_bit_counter_6_a1, n4_bit_counter_6_a2, n4_bit_counter_6_a3,
       n4_seven_segment_1_a_2, n4_seven_segment_1_b_2, n4_seven_segment_1_c_2, n4_seven_segment_1_d_2,
       n4_seven_segment_1_e, n4_seven_segment_1_f, n4_seven_segment_1_g, n4_seven_segment_2_a_2,
       n4_seven_segment_2_b_2, n4_seven_segment_2_c_2, n4_seven_segment_2_d_2, n4_seven_segment_2_e,
       n4_seven_segment_2_f, n4_seven_segment_2_g, n4_seven_segment_3_a_2, n4_seven_segment_3_b_2,
       n4_seven_segment_3_c_2, n4_seven_segment_3_d_2, n4_seven_segment_3_e, n4_seven_segment_3_f,
       n4_seven_segment_3_g, n4_seven_segment_4_a_2, n4_seven_segment_4_b_2, n4_seven_segment_4_c_2,
       n4_seven_segment_4_d_2, n4_seven_segment_4_e, n4_seven_segment_4_f, n4_seven_segment_4_g,
       n4_seven_segment_5_a_2, n4_seven_segment_5_b_2, n4_seven_segment_5_c_2, n4_seven_segment_5_d_2,
       n4_seven_segment_5_e, n4_seven_segment_5_f, n4_seven_segment_5_g, n4_seven_segment_6_a_2,
       n4_seven_segment_6_b_2, n4_seven_segment_6_c_2, n4_seven_segment_6_d_2, n4_seven_segment_6_e,
       n4_seven_segment_6_f, n4_seven_segment_6_g, or_1_out, or_2_out, or_3_out;

  and and_1 (and_1_out, n4_bit_counter_2_a2, n4_bit_counter_1_a1);
  _7_Segment_Display u_7_segment_display_1 (
    .g(n4_seven_segment_1_g), .f(n4_seven_segment_1_f), .a(n4_seven_segment_1_a_2),
    .b(n4_seven_segment_1_b_2), .e(n4_seven_segment_1_e), .d(n4_seven_segment_1_d_2),
    .c(n4_seven_segment_1_c_2));  // open: dp
  _4_seven_segment u_4_seven_segment_1 (
    .A(n4_bit_counter_1_a3), .B(n4_bit_counter_1_a2), .C(n4_bit_counter_1_a1), .D(n4_bit_counter_1_a0),
    .a_2(n4_seven_segment_1_a_2), .b_2(n4_seven_segment_1_b_2), .c_2(n4_seven_segment_1_c_2),
    .d_2(n4_seven_segment_1_d_2), .e(n4_seven_segment_1_e), .f(n4_seven_segment_1_f), .g(n4_seven_segment_1_g));
  _4_bit_counter u_4_bit_counter_1 (
    .T(and_2_out), .Reset(and_1_out), .A3(n4_bit_counter_1_a3), .A2(n4_bit_counter_1_a2),
    .A1(n4_bit_counter_1_a1), .A0(n4_bit_counter_1_a0));
  or or_1 (or_1_out, and_2_out, and_1_out);
  _7_Segment_Display u_7_segment_display_2 (
    .g(n4_seven_segment_2_g), .f(n4_seven_segment_2_f), .a(n4_seven_segment_2_a_2),
    .b(n4_seven_segment_2_b_2), .e(n4_seven_segment_2_e), .d(n4_seven_segment_2_d_2),
    .c(n4_seven_segment_2_c_2));  // open: dp
  _4_seven_segment u_4_seven_segment_2 (
    .A(n4_bit_counter_2_a3), .B(n4_bit_counter_2_a2), .C(n4_bit_counter_2_a1), .D(n4_bit_counter_2_a0),
    .a_2(n4_seven_segment_2_a_2), .b_2(n4_seven_segment_2_b_2), .c_2(n4_seven_segment_2_c_2),
    .d_2(n4_seven_segment_2_d_2), .e(n4_seven_segment_2_e), .f(n4_seven_segment_2_f), .g(n4_seven_segment_2_g));
  and and_2 (and_2_out, n4_bit_counter_2_a3, n4_bit_counter_2_a1);
  _4_bit_counter u_4_bit_counter_2 (
    .T(or_2_out), .Reset(or_1_out), .A3(n4_bit_counter_2_a3), .A2(n4_bit_counter_2_a2),
    .A1(n4_bit_counter_2_a1), .A0(n4_bit_counter_2_a0));
  or or_2 (or_2_out, and_3_out, button_1_out);
  and and_3 (and_3_out, n4_bit_counter_3_a2, n4_bit_counter_3_a1);
  Button button_1 (.out(button_1_out));
  _7_Segment_Display u_7_segment_display_3 (
    .g(n4_seven_segment_3_g), .f(n4_seven_segment_3_f), .a(n4_seven_segment_3_a_2),
    .b(n4_seven_segment_3_b_2), .e(n4_seven_segment_3_e), .d(n4_seven_segment_3_d_2),
    .c(n4_seven_segment_3_c_2));  // open: dp
  _4_seven_segment u_4_seven_segment_3 (
    .A(n4_bit_counter_3_a3), .B(n4_bit_counter_3_a2), .C(n4_bit_counter_3_a1), .D(n4_bit_counter_3_a0),
    .a_2(n4_seven_segment_3_a_2), .b_2(n4_seven_segment_3_b_2), .c_2(n4_seven_segment_3_c_2),
    .d_2(n4_seven_segment_3_d_2), .e(n4_seven_segment_3_e), .f(n4_seven_segment_3_f), .g(n4_seven_segment_3_g));
  _4_bit_counter u_4_bit_counter_3 (
    .T(and_4_out), .Reset(and_3_out), .A3(n4_bit_counter_3_a3), .A2(n4_bit_counter_3_a2),
    .A1(n4_bit_counter_3_a1), .A0(n4_bit_counter_3_a0));
  _7_Segment_Display u_7_segment_display_4 (
    .g(n4_seven_segment_4_g), .f(n4_seven_segment_4_f), .a(n4_seven_segment_4_a_2),
    .b(n4_seven_segment_4_b_2), .e(n4_seven_segment_4_e), .d(n4_seven_segment_4_d_2),
    .c(n4_seven_segment_4_c_2));  // open: dp
  _4_seven_segment u_4_seven_segment_4 (
    .A(n4_bit_counter_4_a3), .B(n4_bit_counter_4_a2), .C(n4_bit_counter_4_a1), .D(n4_bit_counter_4_a0),
    .a_2(n4_seven_segment_4_a_2), .b_2(n4_seven_segment_4_b_2), .c_2(n4_seven_segment_4_c_2),
    .d_2(n4_seven_segment_4_d_2), .e(n4_seven_segment_4_e), .f(n4_seven_segment_4_f), .g(n4_seven_segment_4_g));
  _4_bit_counter u_4_bit_counter_4 (
    .T(or_3_out), .Reset(and_4_out), .A3(n4_bit_counter_4_a3), .A2(n4_bit_counter_4_a2),
    .A1(n4_bit_counter_4_a1), .A0(n4_bit_counter_4_a0));
  and and_4 (and_4_out, n4_bit_counter_4_a3, n4_bit_counter_4_a1);
  or or_3 (or_3_out, and_5_out, button_2_out);
  and and_5 (and_5_out, n4_bit_counter_5_a2, n4_bit_counter_5_a1);
  Button button_2 (.out(button_2_out));
  _7_Segment_Display u_7_segment_display_5 (
    .g(n4_seven_segment_5_g), .f(n4_seven_segment_5_f), .a(n4_seven_segment_5_a_2),
    .b(n4_seven_segment_5_b_2), .e(n4_seven_segment_5_e), .d(n4_seven_segment_5_d_2),
    .c(n4_seven_segment_5_c_2));  // open: dp
  _4_seven_segment u_4_seven_segment_5 (
    .A(n4_bit_counter_5_a3), .B(n4_bit_counter_5_a2), .C(n4_bit_counter_5_a1), .D(n4_bit_counter_5_a0),
    .a_2(n4_seven_segment_5_a_2), .b_2(n4_seven_segment_5_b_2), .c_2(n4_seven_segment_5_c_2),
    .d_2(n4_seven_segment_5_d_2), .e(n4_seven_segment_5_e), .f(n4_seven_segment_5_f), .g(n4_seven_segment_5_g));
  _4_bit_counter u_4_bit_counter_5 (
    .T(and_6_out), .Reset(and_5_out), .A3(n4_bit_counter_5_a3), .A2(n4_bit_counter_5_a2),
    .A1(n4_bit_counter_5_a1), .A0(n4_bit_counter_5_a0));
  and and_6 (and_6_out, n4_bit_counter_6_a3, n4_bit_counter_6_a1);
  _7_Segment_Display u_7_segment_display_6 (
    .g(n4_seven_segment_6_g), .f(n4_seven_segment_6_f), .a(n4_seven_segment_6_a_2),
    .b(n4_seven_segment_6_b_2), .e(n4_seven_segment_6_e), .d(n4_seven_segment_6_d_2),
    .c(n4_seven_segment_6_c_2));  // open: dp
  _4_seven_segment u_4_seven_segment_6 (
    .A(n4_bit_counter_6_a3), .B(n4_bit_counter_6_a2), .C(n4_bit_counter_6_a1), .D(n4_bit_counter_6_a0),
    .a_2(n4_seven_segment_6_a_2), .b_2(n4_seven_segment_6_b_2), .c_2(n4_seven_segment_6_c_2),
    .d_2(n4_seven_segment_6_d_2), .e(n4_seven_segment_6_e), .f(n4_seven_segment_6_f), .g(n4_seven_segment_6_g));
  _4_bit_counter u_4_bit_counter_6 (
    .T(clock_1_out), .Reset(and_6_out), .A3(n4_bit_counter_6_a3), .A2(n4_bit_counter_6_a2),
    .A1(n4_bit_counter_6_a1), .A0(n4_bit_counter_6_a0));
  Clock clock_1 (.out(clock_1_out));

  // Notes on the sheet:
  //   Hours
  //   DIGITAL CLOCK
  //   Minute
  //   Second
endmodule

module _4_seven_segment (
  input  A,
  input  B,
  input  C,
  input  D,
  output a_2,
  output b_2,
  output c_2,
  output d_2,
  output e,
  output f,
  output g
);

  wire and_1_out, and_2_out, and_3_out, and_4_out, and_5_out, and_6_out, and_7_out, and_8_out, and_9_out,
       and_10_out, and_11_out, and_12_out, and_13_out, and_14_out, and_15_out, and_16_out, and_17_out,
       and_18_out, and_19_out, and_20_out, and_21_out, and_22_out, and_23_out, and_24_out, and_25_out,
       and_26_out, and_27_out, and_28_out, and_29_out, and_30_out, and_31_out, and_32_out, and_33_out,
       and_34_out, and_35_out, not_1_out, not_2_out, not_3_out, not_4_out, not_5_out, not_6_out, not_7_out,
       not_8_out, not_9_out, not_10_out, not_11_out, not_12_out, not_13_out, not_14_out, not_15_out,
       not_16_out, not_17_out, not_18_out, not_19_out, not_20_out, not_21_out, not_22_out, not_23_out,
       not_24_out, not_25_out, not_26_out, not_27_out, not_28_out, not_29_out, not_30_out, not_31_out,
       not_32_out, not_33_out, not_34_out, not_35_out, not_36_out, not_37_out, not_38_out, not_39_out,
       not_40_out, not_41_out, not_42_out, not_43_out;

  not not_1 (not_1_out, B);
  and and_1 (and_1_out, not_1_out, not_2_out);
  not not_2 (not_2_out, D);
  not not_3 (not_3_out, A);
  and and_2 (and_2_out, not_3_out, C);
  not not_4 (not_4_out, A);
  and and_3 (and_3_out, not_4_out, B, D);
  and and_4 (and_4_out, B, C);
  and and_5 (and_5_out, A, not_5_out, not_6_out);
  not not_5 (not_5_out, B);
  not not_6 (not_6_out, C);
  and and_6 (and_6_out, A, not_7_out);
  not not_7 (not_7_out, D);
  not not_8 (not_8_out, A);
  and and_7 (and_7_out, not_8_out, not_9_out);
  not not_9 (not_9_out, B);
  not not_10 (not_10_out, A);
  and and_8 (and_8_out, not_10_out, not_11_out, not_12_out);
  not not_11 (not_11_out, C);
  not not_12 (not_12_out, D);
  not not_13 (not_13_out, B);
  and and_9 (and_9_out, not_13_out, not_14_out);
  not not_14 (not_14_out, D);
  not not_15 (not_15_out, A);
  and and_10 (and_10_out, not_15_out, C, D);
  not not_16 (not_16_out, C);
  and and_11 (and_11_out, A, not_16_out, D);
  not not_17 (not_17_out, A);
  and and_12 (and_12_out, not_17_out, not_18_out);
  not not_18 (not_18_out, C);
  not not_19 (not_19_out, A);
  and and_13 (and_13_out, not_19_out, D);
  not not_20 (not_20_out, C);
  and and_14 (and_14_out, not_20_out, D);
  not not_21 (not_21_out, A);
  and and_15 (and_15_out, not_21_out, B);
  and and_16 (and_16_out, A, not_22_out);
  not not_22 (not_22_out, B);
  not not_23 (not_23_out, A);
  and and_17 (and_17_out, not_23_out, not_24_out, not_25_out);
  not not_24 (not_24_out, B);
  not not_25 (not_25_out, D);
  not not_26 (not_26_out, B);
  and and_18 (and_18_out, not_26_out, C, D);
  not not_27 (not_27_out, C);
  and and_19 (and_19_out, B, not_27_out, D);
  and and_20 (and_20_out, B, C, not_28_out);
  not not_28 (not_28_out, D);
  and and_21 (and_21_out, A, not_29_out);
  not not_29 (not_29_out, C);
  not not_30 (not_30_out, B);
  and and_22 (and_22_out, not_30_out, not_31_out);
  not not_31 (not_31_out, D);
  and and_23 (and_23_out, C, not_32_out);
  not not_32 (not_32_out, D);
  and and_24 (and_24_out, A, C);
  and and_25 (and_25_out, A, B);
  not not_33 (not_33_out, C);
  and and_26 (and_26_out, not_33_out, not_34_out);
  not not_34 (not_34_out, D);
  not not_35 (not_35_out, A);
  and and_27 (and_27_out, not_35_out, B, not_36_out);
  not not_36 (not_36_out, C);
  and and_28 (and_28_out, B, not_37_out);
  not not_37 (not_37_out, D);
  and and_29 (and_29_out, A, not_38_out);
  not not_38 (not_38_out, B);
  and and_30 (and_30_out, A, C);
  not not_39 (not_39_out, B);
  and and_31 (and_31_out, not_39_out, C);
  and and_32 (and_32_out, C, not_40_out);
  not not_40 (not_40_out, D);
  not not_41 (not_41_out, A);
  and and_33 (and_33_out, not_41_out, B, not_42_out);
  not not_42 (not_42_out, C);
  and and_34 (and_34_out, A, not_43_out);
  not not_43 (not_43_out, B);
  and and_35 (and_35_out, A, D);
  or or_1 (b_2, and_7_out, and_8_out, and_9_out, and_10_out, and_11_out);
  or or_2 (c_2, and_12_out, and_13_out, and_14_out, and_15_out, and_16_out);
  or or_3 (d_2, and_17_out, and_18_out, and_19_out, and_20_out, and_21_out);
  or or_4 (e, and_22_out, and_23_out, and_24_out, and_25_out);
  or or_5 (f, and_26_out, and_27_out, and_28_out, and_29_out, and_30_out);
  or or_6 (g, and_31_out, and_32_out, and_33_out, and_34_out, and_35_out);
  or or_7 (a_2, and_1_out, and_2_out, and_3_out, and_4_out, and_5_out, and_6_out);
  _7_Segment_Display u_7_segment_display_1 (.g(g), .f(f), .a(a_2), .b(b_2), .e(e), .d(d_2), .c(c_2));  // open: dp
endmodule

module _4_bit_counter (
  input  T,
  input  Reset,
  output A3,
  output A2,
  output A1,
  output A0
);

  wire t_ff_1_qn, t_ff_2_qn, t_ff_3_qn;

  T_Flip_Flop t_ff_1 (.clk(T), .T(1'b1), .Q(A0), .Qn(t_ff_1_qn), .reset(Reset));  // open: preset, en
  T_Flip_Flop t_ff_2 (.clk(t_ff_1_qn), .T(1'b1), .Q(A1), .Qn(t_ff_2_qn), .reset(Reset));  // open: preset, en
  T_Flip_Flop t_ff_3 (.clk(t_ff_2_qn), .T(1'b1), .Q(A2), .Qn(t_ff_3_qn), .reset(Reset));  // open: preset, en
  T_Flip_Flop t_ff_4 (.clk(t_ff_3_qn), .T(1'b1), .Q(A3), .reset(Reset));  // open: Qn, preset, en

  // Notes on the sheet:
  //   4 BIT COUNTER
endmodule
